// Digital circuit Adder Subtractor.dig as structural Verilog
module Adder_Subtractor (
  input  A,
  input  B,
  input  C,
  input  D,
  input  E,
  input  F,
  input  G,
  input  H,
  input  A_S,
  output Y,
  output X,
  output Z,
  output U,
  output Overflow
);

  wire Full_Adder_1_c_o, Full_Adder_2_c_o, Full_Adder_3_c_o, Full_Adder_4_c_o, multiplexer_1_out,
       multiplexer_2_out, multiplexer_3_out, multiplexer_4_out, not_1_out, not_2_out, not_3_out, not_4_out;

  xor xor_1 (Overflow, Full_Adder_4_c_o, Full_Adder_3_c_o);
  Add Full_Adder_4 (.a(multiplexer_1_out), .b(E), .c_i(Full_Adder_3_c_o), .s(Y), .c_o(Full_Adder_4_c_o));
  Add Full_Adder_3 (.a(multiplexer_2_out), .b(F), .c_i(Full_Adder_2_c_o), .s(X), .c_o(Full_Adder_3_c_o));
  Add Full_Adder_2 (.a(multiplexer_3_out), .b(G), .c_i(Full_Adder_1_c_o), .s(Z), .c_o(Full_Adder_2_c_o));
  Add Full_Adder_1 (.a(multiplexer_4_out), .b(H), .c_i(A_S), .s(U), .c_o(Full_Adder_1_c_o));
  Multiplexer multiplexer_1 (.sel(A_S), .in_0(A), .in_1(not_1_out), .out(multiplexer_1_out));
  not not_1 (not_1_out, A);
  Multiplexer multiplexer_2 (.sel(A_S), .in_0(B), .in_1(not_2_out), .out(multiplexer_2_out));
  not not_2 (not_2_out, B);
  Multiplexer multiplexer_3 (.sel(A_S), .in_0(C), .in_1(not_3_out), .out(multiplexer_3_out));
  not not_3 (not_3_out, C);
  Multiplexer multiplexer_4 (.sel(A_S), .in_0(D), .in_1(not_4_out), .out(multiplexer_4_out));
  not not_4 (not_4_out, D);
endmodule
