// Digital circuit Ripple Carry Adder 2-bit.dig as structural Verilog
module Ripple_Carry_Adder_2_bit (
  input  A,
  input  B,
  input  C,
  input  D,
  output Y,
  output X,
  output Z
);

  wire Full_Adder_1_c_o;

  Add Full_Adder_2 (.a(A), .b(C), .c_i(Full_Adder_1_c_o), .s(X), .c_o(Z));
  Add Full_Adder_1 (.a(B), .b(D), .c_i(1'b0), .s(Y), .c_o(Full_Adder_1_c_o));
endmodule
