// Digital circuit Ripple Carry Adder 4-bit.dig as structural Verilog
module Ripple_Carry_Adder_4_bit (
  input  A,
  input  B,
  input  C,
  input  D,
  input  E,
  input  F,
  input  G,
  input  H,
  output Y,
  output X,
  output Z,
  output U,
  output V
);

  wire Full_Adder_1_c_o, Full_Adder_2_c_o, Full_Adder_3_c_o;

  Add Full_Adder_4 (.a(A), .b(E), .c_i(Full_Adder_3_c_o), .s(Y), .c_o(V));
  Add Full_Adder_3 (.a(B), .b(F), .c_i(Full_Adder_2_c_o), .s(X), .c_o(Full_Adder_3_c_o));
  Add Full_Adder_2 (.a(C), .b(G), .c_i(Full_Adder_1_c_o), .s(Z), .c_o(Full_Adder_2_c_o));
  Add Full_Adder_1 (.a(D), .b(H), .c_i(1'b0), .s(U), .c_o(Full_Adder_1_c_o));
endmodule
