// Digital circuit 1-bit_ALU_1.dig as structural Verilog
module _1_bit_ALU_1 (
  input  A,
  input  B,
  input  A_S,
  output Y
);

  wire multiplexer_1_out, not_1_out;

  Add Full_Adder_1 (.a(multiplexer_1_out), .b(B), .c_i(A_S), .s(Y));  // open: c_o
  Multiplexer multiplexer_1 (.sel(A_S), .in_0(A), .in_1(not_1_out), .out(multiplexer_1_out));
  not not_1 (not_1_out, A);
endmodule
